# Fritzing sketch ESP06 (saved by Fritzing 0.9.3b)
circuit board: 3.88288cm x 3.74367cm
breadboards: 1

parts:
  C1 = Capacitor Polarized [package=cpol-radial-100uf-25v]
  hc-sr1 = hc-sr04
  DS2 = DS18B20 1-Wire Temperature Sensor [part_number=DS18B20]
  DS1 = DS18B20 1-Wire Temperature Sensor [part_number=DS18B20]
  J1 = female pin header, 2 pins [form="♀ (female)"]
  J2 = female pin header, 2 pins [form="♀ (female)"]
  V3 = DC Power [voltage=5]
  R6 = Resistor [tolerance=±5% resistance=10k package="1206 [SMD]"]
  R5 = Resistor [tolerance=±5% resistance=4.7k package="1206 [SMD]"]
  R4 = Resistor [tolerance=±5% resistance=2.2k package="1206 [SMD]"]
  R3 = Resistor [tolerance=±5% resistance=4.7k package="1206 [SMD]"]
  R2 = Resistor [tolerance=±5% resistance=4.7k package="1206 [SMD]"]
  R1 = Resistor [tolerance=±5% resistance=4.7k package="1206 [SMD]"]
  IC1 = Voltage Regulator LM1117 [part_number=TS1117BCW package=sot223]
  J5 = female pin header, 3 pins [form="♀ (female)"]
  J6 = female pin header, 6 pins [form="♀ (female)"]
  J3 = male pin header, 3 pins [form="♂ (male)" part_number="rst / flash"]
  U1 = ESP8266 WiFi Module [part_number=ESP12f]
  C2 = Capacitor [package=0805]
  C3 = Capacitor [package=0805]

nets:
  3.3V: C1.+, DS2.VDD, DS1.VDD, R4.Pin_0, R3.Pin_0, R2.Pin_0, R1.Pin_0, IC1.OUT, J5.pin3, J6.pin6, U1.VCC, U1.CH_PD, C3.1
  GND: C1.-, hc-sr1.GND, DS2.GND, DS1.GND, J1.pin2, R6.Pin_0, IC1.ADJ, J5.pin1, J6.pin1, J3.pin2, U1.GND, U1.GPIO_15, C2.2, C3.2
  5V: hc-sr1.VCC, J1.pin1, IC1.IN, J6.pin4, C2.1
  GPIO3 -> TRIG: hc-sr1.Trig, J6.pin3, U1.RXD
  GPIO1 -> ECHO: hc-sr1.Echo, R6.Pin_1, R5.Pin_0, U1.TXD
  ONE WIRE: DS2.DQ, DS1.DQ, R4.Pin_1, J5.pin2, J6.pin5, U1.GPIO_5
  N1: J2.pin1, V3.V+
  N2: J2.pin2, V3.V-
  N3: R5.Pin_1, J6.pin2
  N4: R3.Pin_1, U1.GPIO_0
  N5: R2.Pin_1, J3.pin3, U1.GPIO_2
  N6: R1.Pin_1, J3.pin1, U1.REST

notes:
  ESP06
  5V
  echo
  trig
  GND
  3.3V
  1w
  gnd
  rst
  flash
